// Logisim project OddNumberCheckerProgram.circ as structural Verilog: 1 circuit, main circuit main
module main (
  input  A1,
  input  B1,
  input  C1,
  input  A2,
  input  B2,
  input  C2,
  output ANSWER1,
  output ANSWER2
);

  wire clock_1_out, clock_2_out, not_1_out, or_1_out;

  not not_1 (not_1_out, B2);
  or or_1 (or_1_out, not_1_out, B2);
  Clock clock_1 (.out(clock_1_out));
  and and_1 (ANSWER1, A1, clock_1_out, C1);
  Clock clock_2 (.out(clock_2_out));
  and and_2 (ANSWER2, A2, or_1_out, clock_2_out, C2);

  // Notes on the sheet:
  //   TRUTH TABLE
  //   A          B         C         INT         ANSWER
  //   0          0          0          0                   0
  //   0         0          1          1                    0
  //   0          1          0          2                   0
  //   0          1          1         3                    0
  //   1          0          0          4                   0
  //   1           0          1          5                  1
  //   1          1          0          6                    0
  //   1          1          1          7                    1
  //   Mohamed Yasser Anwar Mahmoud
  //   Odd Number Checker Program
endmodule
